# Fritzing sketch Ikosaeder (saved by Fritzing 0.8.7b)
perfboards: 1

parts:
  Part3 = Arduino Pro Mini v13
  VCC1 = Battery
  R3 = Resistor [tolerance=±5% resistance=1k package=THT]
  R1 = Resistor [tolerance=±5% resistance=20k package=THT]
  D1 = Rectifier Diode [part_number=1N4001 package="300 mil [THT]"]
  D2 = Rectifier Diode [part_number=1N4001 package="300 mil [THT]"]
  R2 = Resistor [tolerance=±5% resistance=1k package=THT]
  R5 = Resistor [tolerance=±5% resistance=270 package=THT]
  R6 = Resistor [tolerance=±5% resistance=270 package=THT]
  R7 = Resistor [tolerance=±5% resistance=270 package=THT]
  R8 = Resistor [tolerance=±5% resistance=270 package=THT]
  R9 = Resistor [tolerance=±5% resistance=270 package=THT]
  R10 = Resistor [tolerance=±5% resistance=270 package=THT]
  R11 = Resistor [tolerance=±5% resistance=270 package=THT]
  R12 = Resistor [tolerance=±5% resistance=270 package=THT]
  R4 = Resistor [tolerance=±5% resistance=20k package=THT]
  IC1 = DIP - 4 pins [chip_label="Power Up" package="DIP (Dual Inline) [THT]"]
  J1 = female pin header, 8 pins [form="♀ (female)"]
  R13 = Resistor [tolerance=±5% resistance=270 package=THT]
  J2 = single row smd female pin header, 6 pins [form="♀ (female)" part_number="HC-05 (optional)"]
  Q1 = NPN-Transistor [package="TO92 [THT]"]
  Q2 = PNP-Transistor [package="TO92 [THT]"]
  S1 = Pushbutton [part_number=On/Animation package="[THT]"]

nets:
  N1: Part3.VCC, IC1.5V_out, J2.pin1
  N2: Part3.GND, IC1.GND_out, J2.pin2
  N3: Part3.D11_PWM/MOSI, R4.Pin_0
  N4: Part3.D10_PWM/SS, D2.anode
  N5: Part3.D9_PWM, R5.Pin_0
  N6: Part3.D8, R6.Pin_0
  N7: Part3.D7, R7.Pin_0
  N8: Part3.D6_PWM, R8.Pin_0
  N9: Part3.D5_PWM, R9.Pin_0
  N10: Part3.D4, R10.Pin_0
  N11: Part3.D3_PWM, R11.Pin_0
  N12: Part3.D2, R12.Pin_0
  N13: Part3.D1/RX, J2.pin4
  N14: Part3.D0/TX, R13.Pin_0
  N15: VCC1.-, IC1.GND_in, Q1.E, S1.Pin_3, S1.Pin_4
  N16: VCC1.+, R1.Pin_1, Q2.E
  N17: R3.Pin_0, Q1.C
  N18: R3.Pin_1, R1.Pin_0, D1.anode, Q2.B
  N19: D1.cathode, D2.cathode, R2.Pin_0
  N20: R2.Pin_1, S1.Pin_1, S1.Pin_2
  N21: R5.Pin_1, J1.pin2
  N22: R6.Pin_1, J1.pin1
  N23: R7.Pin_1, J1.pin8
  N24: R8.Pin_1, J1.pin7
  N25: R9.Pin_1, J1.pin6
  N26: R10.Pin_1, J1.pin5
  N27: R11.Pin_1, J1.pin4
  N28: R12.Pin_1, J1.pin3
  N29: R4.Pin_1, Q1.B
  N30: IC1.Vcc_in, Q2.C
  N31: R13.Pin_1, J2.pin3

notes:
  Ikosaeder, Auto power off circuit with PullUp from 3V to 5V. jens.hauke@4k2.de
  HC-05 Bluetooth (Optional)
  LED connections
  Power & Animation

custom parts:
  DIP - 4 pins: A DIP stand-in part for whatever IC you want. With 4 pins on a 300mil dual inline package (DIP) footprint.
